# Fritzing sketch 20112 이남균 SDS센터 파일 (saved by Fritzing 0.8.7b)
breadboards: 1

parts:
  부품1 = Arduino Uno (Rev3)
  R1 = Resistor [tolerance=±5% resistance=10k package=THT]
  R2 = Photocell (LDR) [package=THT]

nets:
  N1: 부품1.A1, R1.Pin_1, R2.pin_1
