# Fritzing sketch DHT-11도면 (saved by Fritzing 0.8.7b)
breadboards: 1

parts:
  부품1 = Arduino Uno (Rev3)
  DHT11_1 = DHT11 module

nets:
  GND: 부품1.GND, DHT11_1.GND
  5V: 부품1.5V, DHT11_1.VCC

custom parts:
  DHT11 module: https://cdn-learn.adafruit.com/downloads/pdf/dht.pdf DHT11 black pcb module reference by:https://github.com/adafruit/Fritzing-Library/blob/master/parts/DHT11%20Humitidy%20and%20Temperature%20Sensor.fzpz
